# Fritzing sketch circuit-10 (saved by Fritzing 0.8.7b)
breadboards: 1

parts:
  Part1 = Arduino Uno (Rev3)
  IC1 = L293D [package=THT]
  M1 = DC Motor  # not connected
  VCC1 = Battery block 9V  # not connected
  R1 = Rotary Potentiometer (Small) [maximum_resistance=100kΩ package=THT]
  R2 = Resistor [tolerance=±5% resistance=10k package=THT]
  R3 = Resistor [tolerance=±5% resistance=10k package=THT]
  S1 = Pushbutton [package=THT]
  S2 = Pushbutton [package=THT]

nets:
  N1: Part1.A0, R1.wiper
  N2: Part1.5V, IC1.+V, R1.leg2, S1.leg1, S2.leg1
  N3: Part1.GND, R1.leg1, R2.Pin_0, R3.Pin_0
  N4: R3.Pin_1, S1.leg0
